# Fritzing sketch Feather RTC Clock (saved by Fritzing 0.9.3b)

parts:
  Part1 = Adafruit 7 Segment FeatherWing - Blue [part_number="Adafruit #3106"]  # not connected
  Part2 = Adafruit Feather 32u4 Adalogger [part_number="Adafruit #2795"]  # not connected
  Part3 = Adafruit Precision RTC FeatherWing [part_number="Adafruit #3028"]
  S1 = Toggle Switch [package=THT]
  S2 = Pushbutton [package="[THT]"]
  Part5 = Lithium Ion Polymer Battery 3.7v 500mAh [part_number=1578]  # not connected

nets:
  N1: Part3.A, S2.Pin_3, S2.Pin_4
  N2: Part3.GND, S1.COM, S2.Pin_1, S2.Pin_2
  N3: Part3.EN, S1.L1

notes:
  Seven-Segement FeatherWing is plugged into Stacking Headers on Feather 32u4 Adalogger
  Feather 32u4 Adalogger is plugged into female headers on DS3231 Precision RTC FeatherWing
  Battery Plugged into JST on Feather 32u4 Adalogger
  Switch is On/Off wired to EN and GND
  Button is pulled up and used for displaying date

custom parts:
  Adafruit 7 Segment FeatherWing - Blue: One segment? No way dude! 7-Segments for life! This is the Blue Adafruit 0.56" 4-Digit 7-Segment Display w/ FeatherWing Combo Pack! We also have these combo packs in Green, Red, White, and Yellow! 7-Segment Matrices like these are 'multiplexed' - so to control all the seven-segment LEDs you need 14 pins. That's a lot of pins, and there are driver chips like the MAX7219 that can control a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
  Adafruit Feather 32u4 Adalogger: This is the Adafruit Feather 32u4 Adalogger - our take on an 'all-in-one' datalogger (or data-reader) with built in USB and battery charging. Its an Adafruit Feather 32u4 with a microSD holder ready to rock! We have other boards in the Feather family, check'em out here At the Feather 32u4's heart is at ATmega32u4 clocked at 8 MHz and at 3.3V logic, a chip setup we've had tons of experience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
  Adafruit Precision RTC FeatherWing: A Feather board without ambition is a Feather board without FeatherWings! This is the DS3231 Precision RTC FeatherWing: it adds an extremely accurate I2C-integrated Real Time Clock (RTC) with a Temperature Compensated Crystal Oscillator (TCXO) to any Feather main board. This RTC is the most precise you can get in a small, low power package. Using our Feather Stacking Headers or Feather Female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
  Lithium Ion Polymer Battery 3.7v 500mAh: Lithium ion polymer (also known as 'lipo' or 'lipoly') batteries are thin, light and powerful. The output ranges from 4.2V when completely charged to 3.7V. This battery has a capacity of 500mAh for a total of about 1.9 Wh. The batteries come pre-attached with a genuine 2-pin JST-PH connector as shown and include the necessary protection circuitry.
